// Logisim project LC-2200-16.circ as structural Verilog: 3 circuits, main circuit main
module main (
);

  wire [15:0] ALU_output, controlled_buffer_1_out, register_1_q, register_2_q, register_3_q;

  Register #(.width(16)) register_1 (.D(controlled_buffer_1_out), .Q(register_1_q));  // open: en, clk, clr
  Controlled_Buffer #(.width(16)) controlled_buffer_1 (.in(register_1_q), .out(controlled_buffer_1_out));  // open: en
  Register #(.width(16)) register_2 (.D(controlled_buffer_1_out), .Q(register_2_q));  // open: en, clk, clr
  Register #(.width(16)) register_3 (.D(controlled_buffer_1_out), .Q(register_3_q));  // open: en, clk, clr
  ALU ALU (.A(register_2_q), .B(register_3_q), .Output(ALU_output));  // open: func, DrALU
  Controlled_Buffer #(.width(16)) controlled_buffer_2 (.in(ALU_output), .out(controlled_buffer_1_out));  // open: en
endmodule

module ALU (
  input  [15:0] A,
  input  [15:0] B,
  input  [1:0] func,
  input  DrALU,
  output [15:0] Output
);

  wire [15:0] adder_1_out, adder_2_out, nand_1_out, subtractor_1_out;

  Subtractor #(.width(16)) subtractor_1 (.a(A), .b(B), .out(subtractor_1_out));  // open: bin, bout
  assign nand_1_out = ~(A & B);  // NAND_Gate nand_1, 16 bits wide
  Adder #(.width(16)) adder_1 (.a(A), .b(B), .out(adder_1_out));  // open: cin, cout
  Adder #(.width(16)) adder_2 (.a(16'h1), .b(A), .out(adder_2_out));  // open: cin, cout
  Multiplexer #(.select(2), .width(16)) multiplexer_1 (
    .in0(adder_1_out), .in1(nand_1_out), .in2(subtractor_1_out), .in3(adder_2_out), .out(Output), .sel(func),
    .en(DrALU));
endmodule

module _16Reg (
);

  wire decoder_1_out0, decoder_1_out1, decoder_1_out2, decoder_1_out3, decoder_1_out4, decoder_1_out5,
       decoder_1_out6, decoder_1_out7, decoder_1_out8, decoder_1_out9, decoder_1_out10, decoder_1_out11,
       decoder_1_out12, decoder_1_out13, decoder_1_out14, decoder_1_out15;
  wire [3:0] undriven;

  Decoder #(.select(4)) decoder_1 (
    .out0(decoder_1_out0), .out1(decoder_1_out1), .out2(decoder_1_out2), .out3(decoder_1_out3),
    .out4(decoder_1_out4), .out5(decoder_1_out5), .out6(decoder_1_out6), .out7(decoder_1_out7),
    .out8(decoder_1_out8), .out9(decoder_1_out9), .out10(decoder_1_out10), .out11(decoder_1_out11),
    .out12(decoder_1_out12), .out13(decoder_1_out13), .out14(decoder_1_out14), .out15(decoder_1_out15),
    .sel(undriven));  // open: en
  Register register_1 (.en(decoder_1_out0));  // open: D, Q, clk, clr
  Register register_2 (.en(decoder_1_out4));  // open: D, Q, clk, clr
  Register register_3 (.en(decoder_1_out11));  // open: D, Q, clk, clr
  Register register_4 (.en(decoder_1_out15));  // open: D, Q, clk, clr
  Register register_5 (.en(decoder_1_out1));  // open: D, Q, clk, clr
  Register register_6 (.en(decoder_1_out5));  // open: D, Q, clk, clr
  Register register_7 (.en(decoder_1_out10));  // open: D, Q, clk, clr
  Register register_8 (.en(decoder_1_out14));  // open: D, Q, clk, clr
  Register register_9 (.en(decoder_1_out2));  // open: D, Q, clk, clr
  Register register_10 (.en(decoder_1_out6));  // open: D, Q, clk, clr
  Register register_11 (.en(decoder_1_out9));  // open: D, Q, clk, clr
  Register register_12 (.en(decoder_1_out13));  // open: D, Q, clk, clr
  Register register_13 (.en(decoder_1_out3));  // open: D, Q, clk, clr
  Register register_14 (.en(decoder_1_out7));  // open: D, Q, clk, clr
  Register register_15 (.en(decoder_1_out8));  // open: D, Q, clk, clr
  Register register_16 (.en(decoder_1_out12));  // open: D, Q, clk, clr
endmodule
